# Fritzing sketch rotary-kb (saved by Fritzing 0.9.9b)
breadboards: 1

parts:
  Part1 = Arduino Uno (Rev3)
  RE1 = Rotary Encoder [package=THT]
  C1 = Capacitor [package=cap-pth-small2]
  R1 = Resistor [tolerance=±5% resistance=10k package="2010 [SMD]"]
  R2 = Resistor [tolerance=±5% resistance=10k package="2010 [SMD]"]
  R3 = Resistor [tolerance=±5% resistance=1k package="0805 [SMD]"]
  R4 = Resistor [tolerance=±5% resistance=1k package="0805 [SMD]"]
  C2 = Capacitor [package=cap-pth-small2]
  S1 = Pushbutton [package="[THT]"]

nets:
  N1: Part1.D8, R3.Pin_1, C2.1
  N2: Part1.D11_PWM/MOSI, C1.2, R4.Pin_0
  N3: Part1.GND, RE1.EncoderPinC, C1.1, C2.2, S1.Pin_3, S1.Pin_4
  N4: Part1.D5_PWM, S1.Pin_1, S1.Pin_2
  N5: Part1.5V, R1.Pin_1, R2.Pin_1
  N6: RE1.EncoderPinA, R2.Pin_0, R4.Pin_1
  N7: RE1.EncoderPinB, R1.Pin_0, R3.Pin_0
